# Fritzing sketch main_board_layout_fritzing (saved by Fritzing 0.9.0b)
circuit board: 6cm x 8cm
breadboards: 1

parts:
  Part1 = Spark Core (v1.0)
  JP5 = Header 3 [package=screwterminal-3.5mm-3_lock.007s]
  U1 = Voltage Regulator - 5V [package="TO220 [THT]"]
  S1 = SPST Switch [package=switch-spdt_lock.007s]
  S2 = SPST Switch [package=switch-spdt_lock.007s]
  S3 = SPST Switch [package=switch-spdt_lock.007s]
  S4 = SPST Switch [package=switch-spdt_lock.007s]
  S5 = SPST Switch [package=switch-spdt_lock.007s]

nets:
  N1: Part1.GND, JP5.2, S2.S, S3.S, S4.S
  N2: Part1.D0, S4.O
  N3: Part1.D1, S3.O
  N4: Part1.D2, S2.O
  N5: Part1.D3, JP5.1
  N6: U1.input_voltage, S1.P, S2.P, S3.P, S4.P
  N7: S1.S, S5.P
