# Fritzing sketch main_board_layout_fritzing (saved by Fritzing 0.9.0b)
circuit board: 6cm x 8cm
breadboards: 1

parts:
  Part1 = Spark Core (v1.0)
  U1 = Voltage Regulator - 5V [package="TO220 [THT]"]
  S1 = SPST Switch [package=switch-spdt_lock.007s]
  S2 = SPST Switch [package=switch-spdt_lock.007s]
  S3 = SPST Switch [package=switch-spdt_lock.007s]
  S4 = SPST Switch [package=switch-spdt_lock.007s]
  S5 = SPST Switch [package=switch-spdt_lock.007s]
  S7 = SPST Switch [package=switch-spdt_lock.007s]
  S8 = SPST Switch [package=switch-spdt_lock.007s]
  S9 = SPST Switch [package=switch-spdt_lock.007s]
  S10 = SPST Switch [package=switch-spdt_lock.007s]
  C1 = Capacitor Polarized [package=cpol-radial-100uf-25v]
  C2 = Capacitor [package=cap-pth-small2]
  C3 = Capacitor [package=cap-pth-small2]

nets:
  GND: Part1.GND, U1.GND, S2.S, S3.S, S4.S, S5.O, S7.P, S8.P, S9.P, S10.P, C1.-, C2.1, C3.1
  N1: Part1.VIN, U1.output_voltage, S7.S, S8.O, S9.O, S10.S, C2.2
  N2: Part1.D0, S4.O
  N3: Part1.D1, S3.O
  N4: Part1.D2, S2.O
  N5: Part1.D3, C3.2
  N6: Part1.D4, S9.S
  N7: Part1.D5, S8.S
  N8: Part1.D6, S10.O
  N9: Part1.D7, S7.O
  N10: U1.input_voltage, S1.P, S2.P, S3.P, S4.P, C1.+
  N11: S1.S, S5.P
